// Logisim project Guia_0401_b.circ as structural Verilog: 1 circuit, main circuit main
module main (
  input  X,
  input  Y,
  input  Z,
  output Saida
);

  wire not_1_out, not_2_out, or_1_out;

  not not_1 (not_1_out, X);
  not not_2 (not_2_out, Z);
  or or_1 (or_1_out, not_1_out, Y);
  or or_2 (Saida, or_1_out, not_2_out);
endmodule
