// Logisim project Guia_0401_c.circ as structural Verilog: 1 circuit, main circuit main
module main (
  input  X,
  input  Y,
  input  Z,
  output out_4
);

  wire not_1_out, or_1_out;

  or or_1 (or_1_out, X, not_1_out);
  not not_1 (not_1_out, Y);
  or or_2 (out_4, or_1_out, Z);
endmodule
