// Logisim project Guia_0401_d.circ as structural Verilog: 1 circuit, main circuit main
module main (
  input  X,
  input  Y,
  input  Z,
  output out_4
);

  wire not_1_out, or_1_out;

  or or_1 (or_1_out, X, Y);
  not not_1 (not_1_out, Z);
  and and_1 (out_4, or_1_out, not_1_out);
endmodule
