// Logisim project Guia_0402_d02.circ as structural Verilog: 1 circuit, main circuit main
module main (
  input  x,
  input  y,
  output z
);

  wire nand_1_out, nor_1_out, not_1_out;

  not not_1 (not_1_out, y);
  nand nand_1 (nand_1_out, x, not_1_out);
  nor nor_1 (nor_1_out, x, y);
  or or_1 (z, nand_1_out, nor_1_out);
endmodule
