// Logisim project Guia_0404_b.circ as structural Verilog: 1 circuit, main circuit main
module main (
  input  X,
  input  Y,
  input  Z,
  output S
);

  wire not_1_out, not_2_out, not_3_out, not_4_out, or_1_out, or_2_out, or_3_out, or_4_out;

  not not_1 (not_1_out, Y);
  not not_2 (not_2_out, X);
  not not_3 (not_3_out, X);
  not not_4 (not_4_out, Y);
  or or_1 (or_1_out, X, Y, Z);
  or or_2 (or_2_out, X, not_1_out, Z);
  or or_3 (or_3_out, not_2_out, Y, Z);
  or or_4 (or_4_out, not_3_out, not_4_out, Z);
  and and_1 (S, or_1_out, or_2_out, or_3_out, or_4_out);
endmodule
