// Logisim project Guia_0405_a_SoP.circ as structural Verilog: 1 circuit, main circuit main
module main (
  input  x,
  input  y,
  output s
);

  wire not_1_out;

  not not_1 (not_1_out, y);
  and and_1 (s, x, not_1_out);
endmodule
