// Logisim project Guia_0405_b_SoP.circ as structural Verilog: 1 circuit, main circuit main
module main (
  input  x,
  input  y,
  output s
);

  wire and_1_out, and_2_out, not_1_out;

  not not_1 (not_1_out, x);
  and and_1 (and_1_out, not_1_out, y);
  and and_2 (and_2_out, x, y);
  or or_1 (s, and_1_out, and_2_out);
endmodule
