// Logisim project Guia_0405_c_PoS.circ as structural Verilog: 1 circuit, main circuit main
module main (
  input  x,
  input  y,
  input  z,
  output s
);

  wire not_1_out, not_2_out, not_3_out, or_1_out, or_2_out;

  not not_1 (not_1_out, y);
  not not_2 (not_2_out, x);
  not not_3 (not_3_out, z);
  or or_1 (or_1_out, x, not_1_out, z);
  or or_2 (or_2_out, not_2_out, y, not_3_out);
  and and_1 (s, or_1_out, or_2_out);
endmodule
