// Logisim project Guia_0405_e_PoS.circ as structural Verilog: 1 circuit, main circuit main
module main (
  input  x,
  input  y,
  input  w,
  input  z,
  output s
);

  wire not_1_out, not_2_out, not_3_out, not_4_out, not_5_out, not_6_out, not_7_out, not_8_out, not_9_out,
       not_10_out, not_11_out, not_12_out, or_1_out, or_2_out, or_3_out, or_4_out, or_5_out, or_6_out;

  not not_1 (not_1_out, w);
  not not_2 (not_2_out, y);
  not not_3 (not_3_out, y);
  not not_4 (not_4_out, w);
  not not_5 (not_5_out, z);
  not not_6 (not_6_out, x);
  not not_7 (not_7_out, z);
  not not_8 (not_8_out, x);
  not not_9 (not_9_out, y);
  not not_10 (not_10_out, x);
  not not_11 (not_11_out, y);
  not not_12 (not_12_out, z);
  or or_1 (or_1_out, x, y, not_1_out, z);
  or or_2 (or_2_out, x, not_2_out, w, z);
  or or_3 (or_3_out, x, not_3_out, not_4_out, not_5_out);
  or or_4 (or_4_out, not_6_out, y, w, not_7_out);
  or or_5 (or_5_out, not_8_out, not_9_out, w, z);
  or or_6 (or_6_out, not_10_out, not_11_out, w, not_12_out);
  and and_1 (s, or_1_out, or_2_out, or_3_out, or_4_out, or_5_out, or_6_out);
endmodule
