// Logisim project Guia_0603a.circ as structural Verilog: 1 circuit, main circuit main
module main (
  input  x,
  input  y,
  input  w,
  input  z
);

  wire _1_out, _2_out, _3_out, _4_out, _5_out, _6_out, _7_out, _8_out, _9_out, _10_out, _11_out, _12_out,
       _13_out, _15_out, _16_out, not_1_out, not_2_out, not_3_out, not_4_out;

  not not_1 (not_1_out, y);
  not not_2 (not_2_out, x);
  not not_3 (not_3_out, z);
  not not_4 (not_4_out, w);
  and _1 (_1_out, not_2_out, not_4_out);
  and _10 (_10_out, _1_out, _2_out);
  or _2 (_2_out, z, y);
  and _3 (_3_out, not_4_out, z);
  or _11 (_11_out, _3_out, _4_out);
  and _4 (_4_out, not_2_out, not_1_out);
  and _5 (_5_out, w, not_3_out);
  or _12 (_12_out, _5_out, _6_out);
  and _6 (_6_out, x, not_1_out);
  and _7 (_7_out, not_4_out, not_3_out);
  or _13 (_13_out, _7_out, _8_out);
  and _8 (_8_out, x, y);
  and _9 (_9_out, w, not_3_out);
  and _15 (_15_out, _10_out, _11_out);
  or _16 (_16_out, _11_out, _12_out);
  // OR_Gate _17 has open pins: in0=_12_out, in1=_13_out, out=open
  // AND_Gate _14 has open pins: in0=_13_out, in1=_9_out, out=open
  // AND_Gate _20 has open pins: in0=_15_out, in1=_16_out, out=open

  // Notes on the sheet:
  //   10
  //   1
  //   (1-9) : Conjunções mais internas
  //   /
  //   14
  //   |
  //   |
  //   3
  //   2
  //   Quais são as portas necessárias para montar o restante do circuito?
  //   (10-13) : Conjunções intermediárias inferiores
  //   (14-17) : Conjunções intermediárias superiores
  //   (14-17) : Conjunções intermediárias superiores
  //   18
  //   \
  //   15
  //   11
  //   |
  //   4
  //   f(x,y,w,z) = ( (x' . w') . (z + y) ) . ( (w' . z) + (x' . y') ) . ( (w . z') + (x . y') ) . ( (w' . z') + ( (x . y) ) . (w . z')
  //   19
  //   /
  //   \
  //   12
  //   6
  //   5
  //   20
  //   /
  //   16
  //   13
  //   |
  //   7
  //   \
  //   17
  //   |
  //   8
  //   9
endmodule
