// Logisim project Guia_0603b.circ as structural Verilog: 1 circuit, main circuit main
module main (
  input  x,
  input  y,
  input  w,
  input  z,
  output out_5
);

  wire and_2_out, and_3_out, and_4_out, and_5_out, and_6_out, and_7_out, not_1_out, not_2_out, not_3_out,
       not_4_out, or_1_out, or_2_out;

  not not_1 (not_1_out, x);
  not not_2 (not_2_out, y);
  not not_3 (not_3_out, z);
  not not_4 (not_4_out, w);
  // AND_Gate and_1 has open pins: in0=not_2_out, in1=not_4_out, out=open
  and and_2 (and_2_out, not_1_out, not_2_out);
  and and_3 (and_3_out, and_2_out, z);
  and and_4 (and_4_out, x, not_4_out);
  and and_5 (and_5_out, and_4_out, z);
  and and_6 (and_6_out, x, y);
  and and_7 (and_7_out, and_6_out, w);
  or or_1 (or_1_out, and_3_out, and_5_out);
  or or_2 (or_2_out, and_5_out, and_7_out);
  or or_3 (out_5, or_1_out, or_2_out);
endmodule
