// Logisim project Guia_0603c.circ as structural Verilog: 1 circuit, main circuit main
module main (
  input  x,
  input  y,
  input  w,
  input  z,
  output out_5
);

  wire and_1_out, and_2_out, and_3_out, and_4_out, and_5_out, and_6_out, and_7_out, and_8_out, and_9_out,
       and_10_out, and_11_out, and_12_out, not_1_out, not_2_out, not_3_out, not_4_out, or_1_out, or_2_out,
       or_3_out;

  not not_1 (not_1_out, x);
  not not_2 (not_2_out, y);
  not not_3 (not_3_out, z);
  not not_4 (not_4_out, w);
  and and_1 (and_1_out, x, not_2_out);
  and and_2 (and_2_out, and_1_out, not_3_out);
  and and_3 (and_3_out, not_1_out, not_2_out);
  and and_4 (and_4_out, and_3_out, and_5_out);
  and and_5 (and_5_out, not_4_out, z);
  and and_6 (and_6_out, not_1_out, y);
  and and_7 (and_7_out, and_6_out, and_8_out);
  and and_8 (and_8_out, w, z);
  and and_9 (and_9_out, x, not_2_out);
  and and_10 (and_10_out, and_9_out, z);
  and and_11 (and_11_out, x, y);
  and and_12 (and_12_out, and_11_out, z);
  or or_1 (or_1_out, and_2_out, and_4_out);
  or or_2 (or_2_out, and_7_out, and_10_out);
  or or_3 (or_3_out, or_2_out, and_12_out);
  or or_4 (out_5, or_1_out, or_3_out);
endmodule
