// Logisim project Guia_0604c.circ as structural Verilog: 1 circuit, main circuit main
module main (
  input  x,
  input  y,
  input  w,
  input  z,
  output out_5
);

  wire and_1_out, not_1_out, not_2_out, not_3_out, not_4_out, or_1_out, or_2_out, or_3_out, or_4_out,
       or_5_out, or_6_out, or_7_out, or_8_out;

  not not_1 (not_1_out, y);
  not not_2 (not_2_out, x);
  not not_3 (not_3_out, w);
  not not_4 (not_4_out, z);
  or or_1 (or_1_out, not_2_out, y);
  or or_2 (or_2_out, or_1_out, z);
  or or_3 (or_3_out, x, not_1_out);
  or or_4 (or_4_out, or_3_out, or_5_out);
  or or_5 (or_5_out, not_3_out, z);
  or or_6 (or_6_out, x, not_1_out);
  or or_7 (or_7_out, or_6_out, or_8_out);
  or or_8 (or_8_out, not_3_out, not_4_out);
  and and_1 (and_1_out, or_2_out, or_4_out);
  and and_2 (out_5, and_1_out, or_7_out);
endmodule
