// Logisim project Guia_0604d.circ as structural Verilog: 1 circuit, main circuit main
module main (
  input  x,
  input  y,
  input  w,
  input  z,
  output out_5
);

  wire and_1_out, and_2_out, not_1_out, not_2_out, not_3_out, not_4_out, or_1_out, or_2_out, or_3_out,
       or_4_out, or_5_out, or_6_out, or_7_out, or_8_out, or_9_out, or_10_out;

  not not_1 (not_1_out, y);
  not not_2 (not_2_out, x);
  not not_3 (not_3_out, w);
  not not_4 (not_4_out, z);
  or or_1 (or_1_out, x, w);
  or or_2 (or_2_out, or_1_out, not_4_out);
  or or_3 (or_3_out, y, w);
  or or_4 (or_4_out, or_3_out, not_4_out);
  or or_5 (or_5_out, x, not_1_out);
  or or_6 (or_6_out, or_5_out, or_7_out);
  or or_7 (or_7_out, not_3_out, not_4_out);
  or or_8 (or_8_out, not_2_out, not_1_out);
  or or_9 (or_9_out, or_8_out, or_10_out);
  or or_10 (or_10_out, not_3_out, not_4_out);
  and and_1 (and_1_out, or_2_out, or_4_out);
  and and_2 (and_2_out, or_6_out, or_9_out);
  and and_3 (out_5, and_1_out, and_2_out);
endmodule
