// Logisim project Guia_0607.circ as structural Verilog: 1 circuit, main circuit main
module main (
  input  x,
  input  y,
  input  z,
  output out_4
);

  wire not_1_out, not_2_out, not_3_out, or_1_out;

  not not_1 (not_1_out, y);
  not not_2 (not_2_out, x);
  not not_3 (not_3_out, z);
  or or_1 (or_1_out, x, y);
  or or_2 (out_4, or_1_out, not_3_out);
endmodule
