// Logisim project Guia_0702.circ as structural Verilog: 1 circuit, main circuit main
module main (
  input  a,
  input  b,
  input  sel,
  output s
);

  wire and_1_out, and_2_out, nor_1_out, not_1_out, not_2_out, not_3_out, or_1_out;

  not not_1 (not_1_out, b);
  not not_2 (not_2_out, a);
  not not_3 (not_3_out, sel);
  or or_1 (or_1_out, a, b);
  nor nor_1 (nor_1_out, a, b);
  and and_1 (and_1_out, or_1_out, sel);
  or or_2 (s, and_1_out, and_2_out);
  and and_2 (and_2_out, nor_1_out, not_3_out);
endmodule
