// Logisim project Guia_0705.circ as structural Verilog: 1 circuit, main circuit main
module main (
  input  a,
  input  b,
  input  sel_00,
  input  sel_01,
  input  sel_02,
  output out_6
);

  wire and_1_out, and_2_out, and_3_out, and_4_out, and_5_out, and_6_out, and_7_out, and_8_out, and_9_out,
       and_10_out, and_11_out, and_12_out, and_13_out, and_14_out, and_15_out, and_16_out, and_17_out,
       and_18_out, and_19_out, and_20_out, and_21_out, and_22_out, and_23_out, and_24_out, and_25_out,
       nand_1_out, nor_1_out, not_1_out, not_2_out, not_3_out, not_4_out, not_5_out, or_1_out, or_2_out,
       or_3_out, or_4_out, or_5_out, or_6_out, or_7_out, xnor_1_out, xor_1_out;

  not not_1 (not_1_out, b);
  not not_2 (not_2_out, a);
  not not_3 (not_3_out, sel_00);
  not not_4 (not_4_out, sel_01);
  not not_5 (not_5_out, sel_02);
  and and_1 (and_1_out, a, b);
  and and_2 (and_2_out, not_5_out, not_4_out);
  nand nand_1 (nand_1_out, a, b);
  and and_3 (and_3_out, not_4_out, not_5_out);
  or or_1 (or_1_out, a, b);
  and and_4 (and_4_out, not_5_out, sel_01);
  nor nor_1 (nor_1_out, a, b);
  and and_5 (and_5_out, not_5_out, sel_01);
  xor xor_1 (xor_1_out, a, b);
  and and_6 (and_6_out, sel_02, not_4_out);
  and and_7 (and_7_out, sel_02, not_4_out);
  and and_8 (and_8_out, sel_02, sel_01);
  and and_9 (and_9_out, sel_02, sel_01);
  and and_10 (and_10_out, and_2_out, not_3_out);
  and and_11 (and_11_out, and_10_out, not_2_out);
  and and_12 (and_12_out, and_3_out, sel_00);
  and and_13 (and_13_out, and_12_out, and_1_out);
  and and_14 (and_14_out, and_4_out, not_3_out);
  and and_15 (and_15_out, and_14_out, nand_1_out);
  and and_16 (and_16_out, and_5_out, sel_00);
  and and_17 (and_17_out, and_16_out, or_1_out);
  and and_18 (and_18_out, and_6_out, not_3_out);
  and and_19 (and_19_out, and_18_out, nor_1_out);
  xnor xnor_1 (xnor_1_out, a, b);
  and and_20 (and_20_out, and_7_out, sel_00);
  and and_21 (and_21_out, and_20_out, xor_1_out);
  and and_22 (and_22_out, and_8_out, not_3_out);
  and and_23 (and_23_out, and_22_out, xnor_1_out);
  and and_24 (and_24_out, and_9_out, sel_00);
  and and_25 (and_25_out, and_24_out, b);
  or or_2 (or_2_out, and_11_out, and_13_out);
  or or_3 (or_3_out, and_15_out, and_17_out);
  or or_4 (or_4_out, and_19_out, and_21_out);
  or or_5 (or_5_out, and_23_out, and_25_out);
  or or_6 (or_6_out, or_2_out, or_3_out);
  or or_7 (or_7_out, or_4_out, or_5_out);
  or or_8 (out_6, or_6_out, or_7_out);
endmodule
