// Logisim project Guia_0801.circ as structural Verilog
module half_adder (
  input  a,
  input  b,
  output out_3,
  output out_4
);

  xor xor_1 (out_3, a, b);
  and and_1 (out_4, a, b);
endmodule

module full_adder (
  input  a,
  input  b,
  input  sel,
  output out_4,
  output out_5
);

  wire half_adder_1_out_3, half_adder_1_out_4;

  half_adder half_adder_1 (.a(b), .b(a), .out_3(half_adder_1_out_3), .out_4(half_adder_1_out_4));
  or or_1 (out_4, half_adder_1_out_3, half_adder_1_out_4);
  half_adder half_adder_2 (.a(sel), .b(half_adder_1_out_4), .out_4(out_5));  // open: out_3
endmodule
