// Logisim project Guia_0803.circ as structural Verilog: 3 circuits, main circuit main
// half
module main (
  input  in_1,
  input  in_2
);
endmodule

module half_sub (
  input  a,
  input  b,
  output out_3,
  output out_4
);

  wire not_1_out, not_2_out;

  not not_1 (not_1_out, a);
  not not_2 (not_2_out, b);
  and and_1 (out_4, not_1_out, b);
  xor xor_1 (out_3, a, b);
endmodule

module full_sub (
  input  a,
  input  b,
  input  bin,
  output out_4,
  output out_5
);

  wire half_sub_1_out_3, half_sub_1_out_4, half_sub_2_out_3, not_1_out, not_2_out, not_3_out;

  not not_1 (not_1_out, a);
  not not_2 (not_2_out, b);
  not not_3 (not_3_out, bin);
  half_sub half_sub_1 (.a(b), .b(a), .out_3(half_sub_1_out_3), .out_4(half_sub_1_out_4));
  or or_1 (out_4, half_sub_1_out_3, half_sub_2_out_3);
  half_sub half_sub_2 (.a(bin), .b(half_sub_1_out_4), .out_3(half_sub_2_out_3), .out_4(out_5));
endmodule
