// Logisim project ED_11.circ as structural Verilog
// mealy
module mealy_1110 (
  input  clock,
  input  input__ou_x,
  input  clear,
  output \output 
);

  wire d_ff_1_q, d_ff_2_q, d_ff_2_qn, d_ff_3_q;

  D_Flip_Flop d_ff_1 (.clk(clock), .D(input__ou_x), .Q(d_ff_1_q), .reset(clear));  // open: Qn, preset
  D_Flip_Flop d_ff_2 (.clk(clock), .D(d_ff_1_q), .Q(d_ff_2_q), .Qn(d_ff_2_qn), .reset(clear));  // open: preset
  D_Flip_Flop d_ff_3 (.clk(clock), .D(d_ff_2_q), .Q(d_ff_3_q), .reset(clear));  // open: Qn, preset
  D_Flip_Flop d_ff_4 (.clk(clock), .D(d_ff_3_q), .reset(clear));  // open: Q, Qn, preset
  and and_1 (\output , d_ff_1_q, d_ff_2_qn, d_ff_3_q, input__ou_x);
endmodule

// moore
module moore_1111 (
  input  clock,
  input  input__ou_x,
  input  clear,
  output \output 
);

  wire d_ff_1_q, d_ff_2_q, d_ff_2_qn, d_ff_3_q, d_ff_4_q;

  D_Flip_Flop d_ff_1 (.clk(clock), .D(input__ou_x), .Q(d_ff_1_q), .reset(clear));  // open: Qn, preset
  D_Flip_Flop d_ff_2 (.clk(clock), .D(d_ff_1_q), .Q(d_ff_2_q), .Qn(d_ff_2_qn), .reset(clear));  // open: preset
  D_Flip_Flop d_ff_3 (.clk(clock), .D(d_ff_2_q), .Q(d_ff_3_q), .reset(clear));  // open: Qn, preset
  D_Flip_Flop d_ff_4 (.clk(clock), .D(d_ff_3_q), .Q(d_ff_4_q), .reset(clear));  // open: Qn, preset
  and and_1 (\output , d_ff_1_q, d_ff_2_qn, d_ff_3_q, d_ff_4_q);
endmodule

module mealy_moore_1112 (
  input  \input ,
  input  clear,
  output out_3,
  output out_4
);

  wire clock_1_out;

  Clock clock_1 (.out(clock_1_out));
  mealy_1110 mealy_1110_1 (.clock(clock_1_out), .input__ou_x(\input ), .clear(clear), .\output (out_3));
  moore_1111 moore_1111_1 (.clock(clock_1_out), .input__ou_x(\input ), .clear(clear), .\output (out_4));
endmodule

module FSM_1113 (
  input  \input ,
  input  clear,
  output out_3
);

  wire and_1_out, clock_1_out, d_ff_1_q, d_ff_1_qn, d_ff_2_q, d_ff_3_q, d_ff_3_qn, d_ff_4_q, d_ff_5_qn;

  Clock clock_1 (.out(clock_1_out));
  D_Flip_Flop d_ff_1 (.clk(clock_1_out), .D(\input ), .Q(d_ff_1_q), .Qn(d_ff_1_qn), .reset(clear));  // open: preset
  D_Flip_Flop d_ff_2 (.clk(clock_1_out), .D(d_ff_1_q), .Q(d_ff_2_q), .reset(clear));  // open: Qn, preset
  D_Flip_Flop d_ff_3 (.clk(clock_1_out), .D(d_ff_2_q), .Q(d_ff_3_q), .Qn(d_ff_3_qn), .reset(clear));  // open: preset
  D_Flip_Flop d_ff_4 (.clk(clock_1_out), .D(d_ff_3_q), .Q(d_ff_4_q), .reset(clear));  // open: Qn, preset
  and and_1 (and_1_out, d_ff_1_qn, d_ff_2_q, d_ff_3_qn, d_ff_4_q);
  D_Flip_Flop d_ff_5 (.D(and_1_out), .Qn(d_ff_5_qn), .preset(and_1_out));  // open: clk, Q, reset
  not not_1 (out_3, d_ff_5_qn);
endmodule
