// Logisim project ED14.circ as structural Verilog: 5 circuits, main circuit ED14_Q01
module ED14_Q01 (
  input  \input ,
  input  load,
  input  clear,
  output [5:0] out_4
);

  wire clock_1_out;

  Clock clock_1 (.out(clock_1_out));
  D_Flip_Flop #(.Pre_Clr_Positions("LEGACY"), .enable("true"), .NewFFLayout("false")) d_ff_1 (
    .clk(clock_1_out), .D(\input ), .Q(out_4[5]), .en(load), .reset(clear));  // open: Qn, preset
  D_Flip_Flop #(.Pre_Clr_Positions("LEGACY"), .enable("true"), .NewFFLayout("false")) d_ff_2 (
    .clk(clock_1_out), .D(out_4[5]), .Q(out_4[4]), .en(load), .reset(clear));  // open: Qn, preset
  D_Flip_Flop #(.Pre_Clr_Positions("LEGACY"), .enable("true"), .NewFFLayout("false")) d_ff_3 (
    .clk(clock_1_out), .D(out_4[4]), .Q(out_4[3]), .en(load), .reset(clear));  // open: Qn, preset
  D_Flip_Flop #(.Pre_Clr_Positions("LEGACY"), .enable("true"), .NewFFLayout("false")) d_ff_4 (
    .clk(clock_1_out), .D(out_4[3]), .Q(out_4[2]), .en(load), .reset(clear));  // open: Qn, preset
  D_Flip_Flop #(.Pre_Clr_Positions("LEGACY"), .enable("true"), .NewFFLayout("false")) d_ff_5 (
    .clk(clock_1_out), .D(out_4[2]), .Q(out_4[1]), .en(load), .reset(clear));  // open: Qn, preset
  D_Flip_Flop #(.Pre_Clr_Positions("LEGACY"), .enable("true"), .NewFFLayout("false")) d_ff_6 (
    .clk(clock_1_out), .D(out_4[1]), .Q(out_4[0]), .en(load), .reset(clear));  // open: Qn, preset
endmodule

module ED14_Q02 (
  input  \input ,
  input  load,
  input  clear,
  output [5:0] out_4
);

  wire clock_1_out;

  Clock clock_1 (.out(clock_1_out));
  D_Flip_Flop #(.Pre_Clr_Positions("LEGACY"), .enable("true"), .NewFFLayout("false")) d_ff_1 (
    .clk(clock_1_out), .D(out_4[4]), .Q(out_4[5]), .en(load), .reset(clear));  // open: Qn, preset
  D_Flip_Flop #(.Pre_Clr_Positions("LEGACY"), .enable("true"), .NewFFLayout("false")) d_ff_2 (
    .clk(clock_1_out), .D(out_4[3]), .Q(out_4[4]), .en(load), .reset(clear));  // open: Qn, preset
  D_Flip_Flop #(.Pre_Clr_Positions("LEGACY"), .enable("true"), .NewFFLayout("false")) d_ff_3 (
    .clk(clock_1_out), .D(out_4[2]), .Q(out_4[3]), .en(load), .reset(clear));  // open: Qn, preset
  D_Flip_Flop #(.Pre_Clr_Positions("LEGACY"), .enable("true"), .NewFFLayout("false")) d_ff_4 (
    .clk(clock_1_out), .D(out_4[1]), .Q(out_4[2]), .en(load), .reset(clear));  // open: Qn, preset
  D_Flip_Flop #(.Pre_Clr_Positions("LEGACY"), .enable("true"), .NewFFLayout("false")) d_ff_5 (
    .clk(clock_1_out), .D(out_4[0]), .Q(out_4[1]), .en(load), .reset(clear));  // open: Qn, preset
  D_Flip_Flop #(.Pre_Clr_Positions("LEGACY"), .enable("true"), .NewFFLayout("false")) d_ff_6 (
    .clk(clock_1_out), .D(\input ), .Q(out_4[0]), .en(load), .reset(clear));  // open: Qn, preset
endmodule

module ED14_Q03 (
  input  \input ,
  input  clear,
  output [5:0] out_3
);

  wire clock_1_out, or_1_out;

  Clock clock_1 (.out(clock_1_out));
  D_Flip_Flop #(.Pre_Clr_Positions("LEGACY"), .enable("true"), .NewFFLayout("false")) d_ff_1 (
    .clk(clock_1_out), .D(out_3[4]), .Q(out_3[5]), .en(1'b1), .reset(clear));  // open: Qn, preset
  D_Flip_Flop #(.Pre_Clr_Positions("LEGACY"), .enable("true"), .NewFFLayout("false")) d_ff_2 (
    .clk(clock_1_out), .D(out_3[3]), .Q(out_3[4]), .en(1'b1), .reset(clear));  // open: Qn, preset
  D_Flip_Flop #(.Pre_Clr_Positions("LEGACY"), .enable("true"), .NewFFLayout("false")) d_ff_3 (
    .clk(clock_1_out), .D(out_3[2]), .Q(out_3[3]), .en(1'b1), .reset(clear));  // open: Qn, preset
  D_Flip_Flop #(.Pre_Clr_Positions("LEGACY"), .enable("true"), .NewFFLayout("false")) d_ff_4 (
    .clk(clock_1_out), .D(out_3[1]), .Q(out_3[2]), .en(1'b1), .reset(clear));  // open: Qn, preset
  D_Flip_Flop #(.Pre_Clr_Positions("LEGACY"), .enable("true"), .NewFFLayout("false")) d_ff_5 (
    .clk(clock_1_out), .D(out_3[0]), .Q(out_3[1]), .en(1'b1), .reset(clear));  // open: Qn, preset
  or or_1 (or_1_out, out_3[5], \input );
  D_Flip_Flop #(.Pre_Clr_Positions("LEGACY"), .enable("true"), .NewFFLayout("false")) d_ff_6 (
    .clk(clock_1_out), .D(or_1_out), .Q(out_3[0]), .en(1'b1), .reset(clear));  // open: Qn, preset
endmodule

module ED14_Q04 (
  input  \input ,
  input  clear,
  output [5:0] out_3
);

  wire clock_1_out, or_1_out;

  Clock clock_1 (.out(clock_1_out));
  or or_1 (or_1_out, \input , out_3[0]);
  D_Flip_Flop #(.Pre_Clr_Positions("LEGACY"), .enable("true"), .NewFFLayout("false")) d_ff_1 (
    .clk(clock_1_out), .D(or_1_out), .Q(out_3[5]), .en(1'b1), .reset(clear));  // open: Qn, preset
  D_Flip_Flop #(.Pre_Clr_Positions("LEGACY"), .enable("true"), .NewFFLayout("false")) d_ff_2 (
    .clk(clock_1_out), .D(out_3[5]), .Q(out_3[4]), .en(1'b1), .reset(clear));  // open: Qn, preset
  D_Flip_Flop #(.Pre_Clr_Positions("LEGACY"), .enable("true"), .NewFFLayout("false")) d_ff_3 (
    .clk(clock_1_out), .D(out_3[4]), .Q(out_3[3]), .en(1'b1), .reset(clear));  // open: Qn, preset
  D_Flip_Flop #(.Pre_Clr_Positions("LEGACY"), .enable("true"), .NewFFLayout("false")) d_ff_4 (
    .clk(clock_1_out), .D(out_3[3]), .Q(out_3[2]), .en(1'b1), .reset(clear));  // open: Qn, preset
  D_Flip_Flop #(.Pre_Clr_Positions("LEGACY"), .enable("true"), .NewFFLayout("false")) d_ff_5 (
    .clk(clock_1_out), .D(out_3[2]), .Q(out_3[1]), .en(1'b1), .reset(clear));  // open: Qn, preset
  D_Flip_Flop #(.Pre_Clr_Positions("LEGACY"), .enable("true"), .NewFFLayout("false")) d_ff_6 (
    .clk(clock_1_out), .D(out_3[1]), .Q(out_3[0]), .en(1'b1), .reset(clear));  // open: Qn, preset
endmodule

module ED14_Q05 (
  input  \input ,
  input  clear
);

  wire clock_1_out;

  Clock clock_1 (.out(clock_1_out));
  D_Flip_Flop #(.Pre_Clr_Positions("LEGACY"), .enable("true"), .NewFFLayout("false")) d_ff_1 (
    .clk(clock_1_out), .en(1'b1), .reset(clear));  // open: D, Q, Qn, preset
  Multiplexer #(.select(2), .enable("false")) multiplexer_1 ();  // open: in0, in1, in2, in3, out, sel
  Multiplexer #(.select(2), .enable("false")) multiplexer_2 ();  // open: in0, in1, in2, in3, out, sel
  Multiplexer #(.select(2), .enable("false")) multiplexer_3 ();  // open: in0, in1, in2, in3, out, sel
  Multiplexer #(.select(2), .enable("false")) multiplexer_4 ();  // open: in0, in1, in2, in3, out, sel
  D_Flip_Flop #(.Pre_Clr_Positions("LEGACY"), .enable("true"), .NewFFLayout("false")) d_ff_2 (
    .clk(clock_1_out), .en(1'b1), .reset(clear));  // open: D, Q, Qn, preset
  Multiplexer #(.select(2), .enable("false")) multiplexer_5 ();  // open: in0, in1, in2, in3, out, sel
  Multiplexer #(.select(2), .enable("false")) multiplexer_6 ();  // open: in0, in1, in2, in3, out, sel
  D_Flip_Flop #(.Pre_Clr_Positions("LEGACY"), .enable("true"), .NewFFLayout("false")) d_ff_3 (
    .clk(clock_1_out), .en(1'b1), .reset(clear));  // open: D, Q, Qn, preset
  D_Flip_Flop #(.Pre_Clr_Positions("LEGACY"), .enable("true"), .NewFFLayout("false")) d_ff_4 (
    .clk(clock_1_out), .en(1'b1), .reset(clear));  // open: D, Q, Qn, preset
  D_Flip_Flop #(.Pre_Clr_Positions("LEGACY"), .enable("true"), .NewFFLayout("false")) d_ff_5 (
    .clk(clock_1_out), .en(1'b1), .reset(clear));  // open: D, Q, Qn, preset
  D_Flip_Flop #(.Pre_Clr_Positions("LEGACY"), .enable("true"), .NewFFLayout("false")) d_ff_6 (
    .clk(clock_1_out), .en(1'b1), .reset(clear));  // open: D, Q, Qn, preset
endmodule
