// Logisim project Q02-c.circ as structural Verilog: 1 circuit, main circuit main
module main (
  input  A,
  input  B,
  input  C,
  input  D,
  output out_5
);

  wire and_1_out, and_2_out, nand_1_out, nand_2_out, nand_3_out, nand_4_out, or_1_out, or_2_out, or_3_out,
       or_4_out;

  nand nand_1 (nand_1_out, A, A);
  nand nand_2 (nand_2_out, C, C);
  nand nand_3 (nand_3_out, B, B);
  nand nand_4 (nand_4_out, D, D);
  or or_1 (or_1_out, C, D);
  and and_1 (and_1_out, or_1_out, or_2_out);
  or or_2 (or_2_out, A, B, C);
  or or_3 (or_3_out, nand_1_out, nand_3_out, nand_2_out);
  and and_2 (and_2_out, or_3_out, or_4_out);
  or or_4 (or_4_out, nand_3_out, nand_2_out, D);
  and and_3 (out_5, and_1_out, and_2_out);
endmodule
