// Logisim project Q02-d.circ as structural Verilog: 1 circuit, main circuit main
module main (
  input  A,
  input  B,
  input  C,
  output out_4
);

  wire multiplexer_1_out, multiplexer_2_out, nand_1_out, nand_2_out, nand_3_out;

  nand nand_1 (nand_1_out, A, A);
  nand nand_2 (nand_2_out, B, B);
  nand nand_3 (nand_3_out, C, C);
  Multiplexer #(.enable("false")) multiplexer_1 (.in0(A), .in1(nand_2_out), .out(multiplexer_1_out), .sel(A));
  Multiplexer #(.enable("false")) multiplexer_2 (.in0(A), .in1(nand_3_out), .out(multiplexer_2_out), .sel(A));
  Multiplexer #(.enable("false")) multiplexer_3 (
    .in0(multiplexer_1_out), .in1(multiplexer_2_out), .out(out_4), .sel(B));
endmodule
