// Logisim project Q03.circ as structural Verilog: 1 circuit, main circuit main
module main (
  input  A,
  input  B,
  input  C,
  output out_4
);

  wire and_1_out, not_1_out, not_2_out, not_3_out, or_1_out, or_2_out, or_3_out;

  not not_1 (not_1_out, A);
  not not_2 (not_2_out, B);
  not not_3 (not_3_out, C);
  or or_1 (or_1_out, not_1_out, C);
  and and_1 (and_1_out, or_1_out, or_2_out);
  or or_2 (or_2_out, A, B);
  or or_3 (or_3_out, B, C);
  and and_2 (out_4, and_1_out, or_3_out);
endmodule
